# Fritzing sketch ArduinoISP (saved by Fritzing 0.9.2b)
breadboards: 1

parts:
  Bauteil1 = Arduino Uno (Rev3)
  LED1 = LED - 5mm [color="Yellow (595nm)" package="5 mm [THT]"]
  R1 = Resistor [tolerance=±5% resistance=220 package=THT]
  LED2 = LED - 5mm [color="Red (633nm)" package="5 mm [THT]"]
  LED3 = LED - 5mm [color="Green (555nm)" package="5 mm [THT]"]
  R2 = Resistor [tolerance=±5% resistance=220 package=THT]
  R3 = Resistor [tolerance=±5% resistance=220 package=THT]
  C1 = Ceramic Capacitor [capacitance=100nF package="100 mil [THT, multilayer]"]
  J2 = female pin header, 3 pins [form="♀ (female)"]
  J3 = female pin header, 3 pins [form="♀ (female)"]
  J4 = female pin header, 3 pins [form="♀ (female)"]  # not connected
  J5 = female pin header, 3 pins [form="♀ (female)"]  # not connected

nets:
  N1: Bauteil1.D8, R2.Pin_1
  N2: Bauteil1.D9_PWM, R3.Pin_1
  N3: Bauteil1.D10_PWM/SS, J2.pin1
  N4: Bauteil1.D11_PWM/MOSI, J3.pin2
  N5: Bauteil1.D12/MISO, J2.pin3
  N6: Bauteil1.D13/SCK, J2.pin2
  N7: Bauteil1.D7, R1.Pin_1
  N8: Bauteil1.5V, C1.1, J3.pin3
  N9: Bauteil1.GND, LED1.cathode, LED2.cathode, LED3.cathode, C1.0, J3.pin1
  N10: LED1.anode, R1.Pin_0
  N11: LED2.anode, R2.Pin_0
  N12: LED3.anode, R3.Pin_0

notes:
  ICSP
  5V
  MOSI
  GND
  Reset
  SCK
  MISO
